# Fritzing sketch FullArduinoHouse (saved by Fritzing 0.9.5d)
perfboards: 4
stripboards: 4

parts:
  ZS-042_RTC1 = ZS-042 RTC Module
  R9 = Resistor [tolerance=±5% resistance=47k package=THT]
  2N3904 = NPN-Transistor [package="TO92 [THT]"]
  R10 = Resistor [tolerance=±5% resistance=100k package=THT]
  R11 = Resistor [tolerance=±5% resistance=10k package=THT]
  R12 = Resistor [tolerance=±5% resistance=10k package=THT]
  J13 = female pin header, 15 pins [form="♀ (female)"]
  J14 = female pin header, 15 pins [form="♀ (female)"]
  5V = Voltage Regulator - 5V [package="TO220 [THT]"]
  3_3V = Voltage Regulator - 3.3V [package="TO220 [THT]"]
  ToMosFet = female pin header, 4 pins [form="♀ (female)"]
  MosFet = screw terminal, 6 pins
  FanSocket = male pin header, 3 pins [form="♂ (male)"]
  3_3V_2 = male pin header, 2 pins [form="♂ (male)"]
  5V_2 = male pin header, 2 pins [form="♂ (male)"]
  Moisture = male pin header, 4 pins [form="♂ (male)"]
  LightSwitch = male pin header, 3 pins [form="♂ (male)"]
  SHT31 = male pin header, 5 pins [form="♂ (male)"]
  DS3231 = male pin header, 6 pins [form="♂ (male)"]
  FromMosfet = male pin header, 2 pins [form="♂ (male)"]
  J15 = female pin header, 15 pins [form="♀ (female)"]
  ToMosFet1 = female pin header, 4 pins [form="♀ (female)"]
  J16 = female pin header, 15 pins [form="♀ (female)"]
  R13 = Resistor [tolerance=±5% resistance=10k package=THT]
  R14 = Resistor [tolerance=±5% resistance=10k package=THT]
  R15 = Resistor [tolerance=±5% resistance=47k package=THT]
  2N3905 = NPN-Transistor [package="TO92 [THT]"]
  R18 = Resistor [tolerance=±5% resistance=100k package=THT]
  FanSocket1 = male pin header, 3 pins [form="♂ (male)"]
  3_3V1 = male pin header, 2 pins [form="♂ (male)"]
  5V1 = male pin header, 2 pins [form="♂ (male)"]
  Moisture1 = male pin header, 4 pins [form="♂ (male)"]
  LightSwitch1 = male pin header, 3 pins [form="♂ (male)"]
  SHT32 = male pin header, 5 pins [form="♂ (male)"]
  DS3232 = male pin header, 6 pins [form="♂ (male)"]
  FromMosfet1 = male pin header, 2 pins [form="♂ (male)"]
  J5 = screw terminal, 3 pins
  U2 = AD5263BRUZ50 on TSSOP-24 DIP Adapter [part_number=AD5263BRUZ50 package="TSSOP-24 on DIP adapter [THT]"]
  104 = Ceramic Capacitor [capacitance=100nF voltage=50V package="100 mil [THT, multilayer]"]
  R21 = Resistor [tolerance=±5% resistance=10k package=THT]
  105 = Ceramic Capacitor [capacitance=1µF voltage=50V package="100 mil [THT, multilayer]"]
  R22 = Resistor [tolerance=±5% resistance=10k package=THT]
  J17 = female pin header, 12 pins [form="♀ (female)"]
  J18 = female pin header, 12 pins [form="♀ (female)"]
  J19 = female pin header, 12 pins [form="♀ (female)"]
  J20 = female pin header, 12 pins [form="♀ (female)"]
  12V = male pin header, 2 pins [form="♂ (male)"]
  AD5263_IN = male pin header, 5 pins [form="♂ (male)"]
  AD5263_OUT = male pin header, 5 pins [form="♂ (male)"]
  AD5263_IN1 = male pin header, 5 pins [form="♂ (male)"]
  12V1 = male pin header, 2 pins [form="♂ (male)"]
  Dimmer = male pin header, 4 pins [form="♂ (male)"]
  Dimmer1 = male pin header, 4 pins [form="♂ (male)"]
  104_2 = Ceramic Capacitor [capacitance=100nF voltage=50V package="100 mil [THT, multilayer]"]
  105_2 = Ceramic Capacitor [capacitance=1µF voltage=50V package="100 mil [THT, multilayer]"]
  CQRTSL25911 = male pin header, 5 pins [form="♂ (male)"]
  Bauteil1 = Arduino Nano 33 IOT
  AD5263_OUT1 = male pin header, 5 pins [form="♂ (male)"]
  CQRTSL25911_1 = male pin header, 5 pins [form="♂ (male)"]

nets:
  GND: ZS-042_RTC1.GND, 2N3904.E, R10.Pin_1, J13.pin1, J13.pin14, J14.pin4, 5V.GND, 3_3V.GND, ToMosFet.pin1, ToMosFet.pin2, MosFet.pin2, MosFet.pin4, MosFet.pin6, FanSocket.pin2, 3_3V_2.pin2, 5V_2.pin2, Moisture.pin3, Moisture.pin4, LightSwitch.pin3, SHT31.pin1, DS3231.pin1, FromMosfet.pin2, J5.pin1, AD5263_OUT.pin1, CQRTSL25911.pin4, Bauteil1.GND, Bauteil1.D13~
  N1: ZS-042_RTC1.VCC, R11.Pin_0, 3_3V.output_voltage, 3_3V_2.pin1, Moisture.pin2, LightSwitch.pin1, SHT31.pin2, DS3231.pin2, J5.pin3, AD5263_OUT.pin2, CQRTSL25911.pin5
  N2: ZS-042_RTC1.SDA, J13.pin8, SHT31.pin4, DS3231.pin4, AD5263_OUT.pin4, CQRTSL25911.pin3, Bauteil1.A4
  N3: ZS-042_RTC1.SCL, J13.pin9, SHT31.pin3, DS3231.pin3, AD5263_OUT.pin3, CQRTSL25911.pin2, Bauteil1.A5
  N4: ZS-042_RTC1.SQW, J14.pin13, DS3231.pin5, Bauteil1.D10~
  N5: ZS-042_RTC1.32K, DS3231.pin6
  N6: R9.Pin_0, 2N3904.B, R10.Pin_0
  N7: R9.Pin_1, R12.Pin_0, FanSocket.pin1
  N8: 2N3904.C, R11.Pin_1, J13.pin5, Bauteil1.A1
  N9: R12.Pin_1, J13.pin15, 5V.output_voltage, MosFet.pin1, MosFet.pin3, FanSocket.pin3, 5V_2.pin1, FromMosfet.pin1, Bauteil1.VIN
  N10: J13.pin2, Bauteil1.3V3
  N11: J13.pin3, Bauteil1.AREF
  N12: J13.pin4, Moisture.pin1, Bauteil1.A0
  N13: J13.pin6, Bauteil1.A2
  N14: J13.pin7, Bauteil1.A3
  N15: J13.pin10, Bauteil1.A6
  N16: J13.pin11, J13.pin13, J14.pin3, Bauteil1.RESET, Bauteil1.A7
  N17: J14.pin1, Bauteil1.TX
  N18: J14.pin2, Bauteil1.RX
  N19: J14.pin5, ToMosFet.pin3, ToMosFet.pin4, MosFet.pin5, Bauteil1.D2
  N20: J14.pin6, LightSwitch.pin2, J5.pin2, Bauteil1.D3~
  N21: J14.pin7, AD5263_OUT.pin5, Bauteil1.D4
  N22: J14.pin8, Bauteil1.D5~
  N23: J14.pin9, Bauteil1.D6~
  N24: J14.pin10, SHT31.pin5, Bauteil1.D7
  N25: J14.pin11, Bauteil1.D8
  N26: J14.pin12, CQRTSL25911.pin1, Bauteil1.D9~
  N27: J14.pin14, Bauteil1.D11/MOSI
  N28: J14.pin15, Bauteil1.D12~/MISO
  12V: 5V.input_voltage, 3_3V.input_voltage, U2.VDD, 105.0, J17.pin7, 12V.pin1
  N29: J15.pin5, ToMosFet1.pin3, ToMosFet1.pin4
  N30: J15.pin6, LightSwitch1.pin2
  N31: J15.pin7, AD5263_OUT1.pin5
  N32: J15.pin10, SHT32.pin5
  N33: J15.pin12, CQRTSL25911_1.pin1
  N34: J15.pin13, DS3232.pin5
  N35: ToMosFet1.pin1, ToMosFet1.pin2, J16.pin14, 2N3905.E, R18.Pin_1, FanSocket1.pin2, 3_3V1.pin2, 5V1.pin2, LightSwitch1.pin3, SHT32.pin1, DS3232.pin1, FromMosfet1.pin2, AD5263_OUT1.pin1, CQRTSL25911_1.pin4
  N36: J16.pin4, Moisture1.pin1
  N37: J16.pin5, R14.Pin_0, 2N3905.C
  N38: J16.pin8, SHT32.pin4, DS3232.pin4, AD5263_OUT1.pin4, CQRTSL25911_1.pin3
  N39: J16.pin9, SHT32.pin3, DS3232.pin3, AD5263_OUT1.pin3, CQRTSL25911_1.pin2
  N40: J16.pin15, 5V1.pin1
  N41: R13.Pin_0, R15.Pin_0, FanSocket1.pin1
  N42: R13.Pin_1, FanSocket1.pin3, FromMosfet1.pin1
  N43: R14.Pin_1, 3_3V1.pin1, Moisture1.pin2, LightSwitch1.pin1, SHT32.pin2, DS3232.pin2, AD5263_OUT1.pin2, CQRTSL25911_1.pin5
  N44: R15.Pin_1, 2N3905.B, R18.Pin_0
  N45: Moisture1.pin3, Moisture1.pin4
  N46: U2.B1, J17.pin1
  N47: U2.A1, U2.B2, J17.pin2, J18.pin12
  N48: U2.W1, J17.pin3, Dimmer.pin3, Dimmer.pin4
  N49: U2.B3, J17.pin4
  N50: U2.A3, J17.pin5
  N51: U2.W3, J17.pin6
  GND_2: U2.GND, U2.CS/AD0, U2.RES/AD1, U2.VSS, 104.0, R21.Pin_1, 105.1, J17.pin8, J18.pin1, J18.pin2, J18.pin6, 12V.pin2, AD5263_IN.pin1
  N52: U2.DIS, U2.VLOGIC, 104.1, J17.pin9, J17.pin10, AD5263_IN.pin2
  N53: U2.SDI/SDA, J17.pin11, AD5263_IN.pin4
  N54: U2.CLK/SCL, J17.pin12, AD5263_IN.pin3
  N55: U2.SHDN, R21.Pin_0, J18.pin3, AD5263_IN.pin5
  N56: U2.SDO/O1, J18.pin4
  N57: U2.NC/O2, J18.pin5
  N58: U2.W4, J18.pin7
  N59: U2.A4, J18.pin8
  N60: U2.B4, J18.pin9
  N61: U2.W2, J18.pin10, Dimmer.pin1, Dimmer.pin2
  N62: U2.A2, J18.pin11
  N63: R22.Pin_0, J19.pin3, AD5263_IN1.pin5
  N64: R22.Pin_1, J19.pin1, J19.pin2, J19.pin6, J20.pin5, 12V1.pin2, 104_2.1, 105_2.0
  N65: J19.pin10, Dimmer1.pin1, Dimmer1.pin2
  N66: J19.pin12, J20.pin11
  N67: J20.pin1, AD5263_IN1.pin3
  N68: J20.pin2, AD5263_IN1.pin4
  N69: J20.pin3, J20.pin4, AD5263_IN1.pin2, 104_2.0
  N70: J20.pin6, 12V1.pin1, 105_2.1
  N71: J20.pin10, Dimmer1.pin3, Dimmer1.pin4

custom parts:
  AD5263BRUZ50 on TSSOP-24 DIP Adapter: Quad 256-position 50 kOhm digital potentiometer on an 18 mm x 30.5 mm TSSOP-24 to DIP adapter. Connector names follow the Analog Devices AD5263 datasheet. Breadboard and PCB views model the adapter pinout: left side pins 1-12 from top to bottom, right side pins 13-24 from bottom to top.
  Arduino Nano 33 IOT: The Arduino Nano 33 IoT is the easiest and cheapest point of entry to enhance existing devices (and creating new ones) to be part of the IoT and designing pico-network applications. Whether you are looking at building a sensor network connected to your office or home router, or if you want to create a BLE device sending data to a cellphone, the Nano 33 IoT is your one-stop-solution for many of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
